# Fritzing sketch I2C_LevelShifter (saved by Fritzing 0.9.2b)

parts:
  Q1 = Basic FET N-Channel [package="TO220 [THT]"]
  Q2 = Basic FET N-Channel [package="TO220 [THT]"]
  R5 = 1.8K Ω Resistor [package=THT]
  R6 = 1.8K Ω Resistor [package=THT]
  Part3 = Mikrobus Prototype Board - 18 v2

nets:
  N1: Q1.gate, Q2.gate, Part3.L3.3-2, Part3.L71, Part3.L72, Part3.L74, Part3.+3.3v-1, Part3.R71, Part3.R74
  N2: Q1.drain, R6.Pin_0, Part3.L81, Part3.L83, Part3.L84, Part3.R21
  N3: Q1.source, Part3.L91, Part3.L93, Part3.L94, Part3.SDA1, Part3.SDA4
  N4: Q2.drain, R5.Pin_0, Part3.R31, Part3.R82, Part3.R83, Part3.R84
  N5: Q2.source, Part3.R93, Part3.R94, Part3.SCL3, Part3.SCL4
  N6: R5.Pin_1, R6.Pin_1, Part3.L11, Part3.L13, Part3.L14, Part3.L61, Part3.L63, Part3.L64, Part3.R+5v-1, Part3.R11, Part3.R61, Part3.R63, Part3.+5v4
  N7: Part3.GND-M8, Part3.R41

notes:
  Raspberry Pi already has pull up resistors
  SDA - 3v Green
  SDA - 5v Purple
  SCL - 3v Yellow
  SCL - 5v Cyan
  3.3v - Orange
  5v - Red
  GND - Black
  MOSFETs IRL2203NPBF N-channel

custom parts:
  1.8K Ω Resistor: A generic resistor (0.25W)
  Mikrobus Prototype Board - 18 v2: Mikrobus Prototype board - 18
