# Fritzing sketch I2C_with_PI_pull_up_Resistors (saved by Fritzing 0.9.2b)
breadboards: 1

parts:
  Part1 = Mikrobus - Cobbler
  Q1 = Basic FET N-Channel [package="TO220 [THT]"]
  Q2 = Basic FET N-Channel [package="TO220 [THT]"]
  R5 = 1.8K Ω Resistor [package=THT]
  R4 = 1.8K Ω Resistor [package=THT]
  R3 = 1.8K Ω Resistor [package=THT]
  R6 = 1.8K Ω Resistor [package=THT]

nets (from the breadboard view):
  N1: Part1.+3.3V, Q1.gate, Q2.gate, R4.Pin_1, R3.Pin_1
  N2: Part1.+5V, R5.Pin_1, R6.Pin_1
  N3: Part1.SDA, Q1.source, R4.Pin_0
  N4: Part1.SCL, Q2.source, R3.Pin_0
  N5: Q1.drain, R6.Pin_0
  N6: Q2.drain, R5.Pin_0

notes:
  Raspberry Pi already has pull up resistors
  SDA - 3v Green
  SDA - 5v Purple
  SCL - 3v Yellow
  SCL - 5v Cyan
  3.3v - Orange
  5v - Red
  GND - Black
  MOSFETs IRL2203NPBF N-channel

custom parts:
  Mikrobus - Cobbler: The idea of the Mikrobus cobbler is to plug it into a breadboard and connect the 40 way connector to the 40 way connector on the Raspberry Pi B+, 2B using a Ribbon cable. You can then prototype your Mikrobus board and test with the Raspberry Pi
  1.8K Ω Resistor: A generic resistor (0.25W)
